// Logisim project hw3.circ as structural Verilog: 7 circuits, main circuit 4-bit ALU
module _4_bit_ALU (
  input  [3:0] A,
  input  [3:0] B,
  input  S0,
  input  S1,
  input  S2,
  output [3:0] Output
);

  wire [3:0] Addition_Output, AND_Output, Decrement_Output, Negation_Output, not_1_out, OR_Output,
       Subtraction_Output, XOR_Output;

  _4_bit_Full_Adder u_4_bit_full_adder_1 (.A(A), .B(B), .CarryIn(1'b0), .Answer(Addition_Output));  // open: CarryOut
  assign OR_Output = A | B;  // OR_Gate or_1, 4 bits wide
  // _4_bit_Subtraction 4_bit_subtraction_1: pin names not known; wires that end beside it: A, 4'b0001, 1'b0, Decrement_Output
  _4_bit_Subtraction u_4_bit_subtraction_2 (.A(A), .B(B), .Output(Subtraction_Output));  // open: CarryOut
  assign not_1_out = ~A;  // NOT_Gate not_1, 4 bits wide
  _4_bit_Full_Adder u_4_bit_full_adder_2 (
    .A(not_1_out), .B(4'b0001), .CarryIn(1'b0), .Answer(Negation_Output));  // open: CarryOut
  assign AND_Output = A & B;  // AND_Gate and_1, 4 bits wide
  assign XOR_Output = A ^ B;  // XOR_Gate xor_1, 4 bits wide
  Multiplexer #(.select(3), .width(4), .disabled(0), .enable("false")) multiplexer_1 (
    .in0(Addition_Output), .in1(Subtraction_Output), .in2(Decrement_Output), .in3(Negation_Output),
    .in4({A[1:0], 2'b00}), .in5(AND_Output), .in6(OR_Output), .in7(XOR_Output), .out(Output),
    .sel({S2, S1, S0}));

  // Other names for the same wires on the sheet: Multiply_4_Output[3:2] = A[1:0]

  // Notes on the sheet:
  //   OR 1 1 0
  //   Connor Lindquist 902990968
  //   Addition 0 0 0
  //   Decrement 0 1 0
  //   Multiply * 4 1 0 0
  //   Subtraction 0 0 1
  //   Negation 0 1 1
  //   AND 1 0 1
  //   XOR 1 1 1
endmodule

module _16_bit_ALU (
  input  [15:0] A,
  input  [15:0] B,
  input  S0,
  input  S1,
  input  S2,
  output [15:0] Output
);

  wire [15:0] Addition_Output, AND_Output, Decrement_Output, n16_bit_full_adder_3_output, Negation_Output,
       not_1_out, not_2_out, not_3_out, OR_Output, Subtraction_Output, XOR_Output;

  _16_bit_Full_Adder u_16_bit_full_adder_1 (.A(A), .B(B), .CarryIn(1'b0), .Output(Addition_Output));  // open: CarryOut
  assign not_1_out = ~{16{1'b0}};  // NOT_Gate not_1, 16 bits wide
  assign OR_Output = A | B;  // OR_Gate or_1, 16 bits wide
  _16_bit_Full_Adder u_16_bit_full_adder_2 (
    .A(A), .B(not_1_out), .CarryIn(1'b0), .Output(Decrement_Output));  // open: CarryOut
  assign not_2_out = ~B;  // NOT_Gate not_2, 16 bits wide
  assign not_3_out = ~A;  // NOT_Gate not_3, 16 bits wide
  assign AND_Output = A & B;  // AND_Gate and_1, 16 bits wide
  assign XOR_Output = A ^ B;  // XOR_Gate xor_1, 16 bits wide
  _16_bit_Full_Adder u_16_bit_full_adder_3 (
    .A({16{1'b0}}), .B(not_2_out), .CarryIn(1'b1), .Output(n16_bit_full_adder_3_output));  // open: CarryOut
  _16_bit_Full_Adder u_16_bit_full_adder_4 (
    .A({16{1'b0}}), .B(not_3_out), .CarryIn(1'b1), .Output(Negation_Output));  // open: CarryOut
  Multiplexer #(.select(3), .width(16), .disabled(0), .enable("false")) multiplexer_1 (
    .in0(Addition_Output), .in1(Subtraction_Output), .in2(Decrement_Output), .in3(Negation_Output),
    .in4({A[13:0], 2'b00}), .in5(AND_Output), .in6(OR_Output), .in7(XOR_Output), .out(Output),
    .sel({S2, S1, S0}));
  _16_bit_Full_Adder u_16_bit_full_adder_5 (
    .A(A), .B(n16_bit_full_adder_3_output), .CarryIn(1'b0), .Output(Subtraction_Output));  // open: CarryOut

  // Other names for the same wires on the sheet: Multiply_4_Output[15:2] = A[13:0]

  // Notes on the sheet:
  //   OR 1 1 0
  //   Connor Lindquist 902990968
  //   Addition 0 0 0
  //   Decrement 0 1 0
  //   Multiply * 4 1 0 0
  //   Subtraction 0 0 1
  //   Negation 0 1 1
  //   AND 1 0 1
  //   XOR 1 1 1
endmodule

module _1_bit_Full_Adder (
  input  A,
  input  B,
  input  CarryIn,
  output Answer,
  output CarryOut
);

  wire and_1_out, and_2_out, xor_1_out;

  xor xor_1 (xor_1_out, A, B);
  and and_1 (and_1_out, CarryIn, xor_1_out);
  and and_2 (and_2_out, B, A);
  xor xor_2 (Answer, xor_1_out, CarryIn);
  or or_1 (CarryOut, and_1_out, and_2_out);

  // Notes on the sheet:
  //   Connor Lindquist 902990968
endmodule

module _4_bit_Full_Adder (
  input  [3:0] A,
  input  [3:0] B,
  input  CarryIn,
  output [3:0] Answer,
  output CarryOut
);

  wire n1_bit_full_adder_1_carryout, n1_bit_full_adder_2_carryout, n1_bit_full_adder_3_carryout;

  _1_bit_Full_Adder u_1_bit_full_adder_1 (
    .A(A[0]), .B(B[0]), .CarryIn(CarryIn), .Answer(Answer[0]), .CarryOut(n1_bit_full_adder_1_carryout));
  _1_bit_Full_Adder u_1_bit_full_adder_2 (
    .A(A[1]), .B(B[1]), .CarryIn(n1_bit_full_adder_1_carryout), .Answer(Answer[1]),
    .CarryOut(n1_bit_full_adder_2_carryout));
  _1_bit_Full_Adder u_1_bit_full_adder_3 (
    .A(A[2]), .B(B[2]), .CarryIn(n1_bit_full_adder_2_carryout), .Answer(Answer[2]),
    .CarryOut(n1_bit_full_adder_3_carryout));
  _1_bit_Full_Adder u_1_bit_full_adder_4 (
    .A(A[3]), .B(B[3]), .CarryIn(n1_bit_full_adder_3_carryout), .Answer(Answer[3]), .CarryOut(CarryOut));

  // Notes on the sheet:
  //   Connor Lindquist 902990968
endmodule

module _4_bit_Subtraction (
  input  [3:0] A,
  input  [3:0] B,
  output [3:0] Output,
  output CarryOut
);

  wire [3:0] n4_bit_full_adder_2_answer, not_1_out;

  assign not_1_out = ~B;  // NOT_Gate not_1, 4 bits wide
  _4_bit_Full_Adder u_4_bit_full_adder_1 (
    .A(A), .B(n4_bit_full_adder_2_answer), .CarryIn(1'b0), .Answer(Output));  // open: CarryOut
  _4_bit_Full_Adder u_4_bit_full_adder_2 (
    .A(not_1_out), .B(4'b0001), .CarryIn(1'b0), .Answer(n4_bit_full_adder_2_answer), .CarryOut(CarryOut));
endmodule

module _1_bit_Subtract (
  input  A,
  input  B,
  input  CarryIn,
  output Output,
  output CarryOut
);

  wire nand_1_out, nand_2_out, not_1_out, not_2_out, not_3_out, not_4_out, xor_1_out;

  not not_1 (not_1_out, A);
  xor xor_1 (xor_1_out, A, B);
  not not_2 (not_2_out, xor_1_out);
  xor xor_2 (Output, xor_1_out, CarryIn);
  nand nand_1 (nand_1_out, not_2_out, CarryIn);
  nand nand_2 (nand_2_out, B, not_1_out);
  not not_3 (not_3_out, nand_1_out);
  not not_4 (not_4_out, nand_2_out);
  or or_1 (CarryOut, not_3_out, not_4_out);
endmodule

module _16_bit_Full_Adder (
  input  CarryIn,
  input  [15:0] A,
  input  [15:0] B,
  output [15:0] Output,
  output CarryOut
);

  wire n4_bit_full_adder_1_carryout, n4_bit_full_adder_2_carryout, n4_bit_full_adder_3_carryout;

  _4_bit_Full_Adder u_4_bit_full_adder_1 (
    .A(A[3:0]), .B(B[3:0]), .CarryIn(CarryIn), .Answer(Output[3:0]), .CarryOut(n4_bit_full_adder_1_carryout));
  _4_bit_Full_Adder u_4_bit_full_adder_2 (
    .A(A[7:4]), .B(B[7:4]), .CarryIn(n4_bit_full_adder_1_carryout), .Answer(Output[7:4]),
    .CarryOut(n4_bit_full_adder_2_carryout));
  _4_bit_Full_Adder u_4_bit_full_adder_3 (
    .A(A[11:8]), .B(B[11:8]), .CarryIn(n4_bit_full_adder_2_carryout), .Answer(Output[11:8]),
    .CarryOut(n4_bit_full_adder_3_carryout));
  _4_bit_Full_Adder u_4_bit_full_adder_4 (
    .A(A[15:12]), .B(B[15:12]), .CarryIn(n4_bit_full_adder_3_carryout), .Answer(Output[15:12]),
    .CarryOut(CarryOut));
endmodule
